# Fritzing sketch BrewBench-wiring-diagram-SSR (saved by Fritzing 0.9.3b)
breadboards: 1

parts:
  Part1 = Arduino Yun
  U6 = Power Outlet [chip_label=IC package="SIP (Single Inline) [THT]"]
  U7 = RELAY-SOLIDSTATE [package=relay-s108t02]
  U8 = RELAY-SOLIDSTATE [package=relay-s108t02]
  R6 = Resistor [tolerance=±5% resistance=10k package=THT]
  DHT2 = DHT11 Humitidy and Temperature Sensor
  R7 = Resistor [tolerance=±5% resistance=10k package=THT]
  R8 = Resistor [tolerance=±5% resistance=10k package=THT]
  R9 = Resistor [tolerance=±5% resistance=10k package=THT]

nets:
  N1: Part1.A0, R9.Pin_1
  N2: Part1.A2, R8.Pin_1
  N3: Part1.A4/SDA, R7.Pin_1
  GND: Part1.GND, U7.-, DHT2.GND
  N4: Part1.D3/SCL, Part1.D3_PWM, U7.+
  N5: Part1.D5_PWM, U8.+
  N6: Part1.D7, R6.Pin_0, DHT2.DATA
  5V: Part1.5V, R6.Pin_1, DHT2.VDD, R7.Pin_0, R8.Pin_0, R9.Pin_0
  N7: U6.hot1, U7.T1
  N8: U6.hot2, U8.T1

notes:
  Hot Liquor
  Mash
  Boil
  10K Resistor
  10K Thermistor
  Heater
  Pump
  3 prong plug
  SSR-40 Solid State Relay
  PWM Port
  < Break Tab
  10K DHT11
  Temp/Humidity

custom parts:
  Power Outlet: A standard power outlet. Silver screws are neutral, brass screws are hot. Green screw is ground.
  DHT11 Humitidy and Temperature Sensor: DHT11 Humidity and Temperature Sensor
