# Fritzing sketch BrewBench-wiring-diagram (saved by Fritzing 0.9.3b)
breadboards: 1

parts:
  Part1 = Arduino Yun
  R1 = Resistor [tolerance=±5% resistance=10k package=THT]
  U6 = Power Outlet [chip_label=IC package="SIP (Single Inline) [THT]"]
  2_Channel_Relay2 = 2 Channel Power Relay
  DHT1 = DHT11 Humitidy and Temperature Sensor
  R2 = Resistor [tolerance=±5% resistance=10k package=THT]  # not connected
  R3 = Resistor [tolerance=±5% resistance=10k package=THT]
  R4 = Resistor [tolerance=±5% resistance=10k package=THT]
  R5 = Resistor [tolerance=±5% resistance=10k package=THT]

nets:
  N1: Part1.A0, R4.Pin_1
  N2: Part1.A2, R3.Pin_1
  N3: Part1.A4/SDA, R1.Pin_1
  5V: Part1.5V, R1.Pin_0, 2_Channel_Relay2.VCC, DHT1.VDD, R3.Pin_0, R4.Pin_0, R5.Pin_1
  GND: Part1.GND, 2_Channel_Relay2.GND, DHT1.GND
  N4: Part1.D2/SDA, Part1.D2, 2_Channel_Relay2.IN1
  N5: Part1.D4, 2_Channel_Relay2.IN2
  N6: Part1.D7, DHT1.DATA, R5.Pin_0
  N7: U6.hot1, 2_Channel_Relay2.K1-NO
  N8: U6.hot2, 2_Channel_Relay2.K2-NO

notes:
  Hot Liquor
  Mash
  Boil
  10K Resistor
  10K Thermistor
  Heater
  Pump
  < Break Tab
  3 prong plug
  10K DHT11
  Temp/Humidity

custom parts:
  Power Outlet: A standard power outlet. Silver screws are neutral, brass screws are hot. Green screw is ground.
  2 Channel Power Relay: A 2 channel power relay. The module operates at 5V.
  DHT11 Humitidy and Temperature Sensor: DHT11 Humidity and Temperature Sensor
