# Fritzing sketch BrewBench-wiring-diagram-SSR (saved by Fritzing 0.9.3b)
breadboards: 1

parts:
  R1 = Resistor [tolerance=±5% resistance=220 package=THT]
  Part1 = Arduino Yun
  R2 = Resistor [tolerance=±5% resistance=220 package=THT]
  R3 = Resistor [tolerance=±5% resistance=220 package=THT]
  U6 = Power Outlet [chip_label=IC package="SIP (Single Inline) [THT]"]
  U7 = RELAY-SOLIDSTATE [package=relay-s108t02]
  U8 = RELAY-SOLIDSTATE [package=relay-s108t02]

nets:
  N1: R1.Pin_0, Part1.5V, R2.Pin_0, R3.Pin_0
  N2: R1.Pin_1, Part1.A0
  N3: Part1.A2, R2.Pin_1
  N4: Part1.A4/SDA, R3.Pin_1
  N5: Part1.D3/SCL, Part1.D3_PWM, U7.+
  N6: Part1.D5_PWM, U8.+
  N7: Part1.GND, U7.-
  N8: U6.hot1, U7.T1
  N9: U6.hot2, U8.T1

notes:
  Hot Liquor
  Mash
  Boil
  10K Resistor
  10K Thermistor
  Heater
  Pump
  3 prong plug
  SSR-40 Solid State Relay
  PWM Port
  < Break Tab

custom parts:
  Power Outlet: A standard power outlet. Silver screws are neutral, brass screws are hot. Green screw is ground.
